# Fritzing sketch arduilamp (saved by Fritzing 0.9.4)
circuit board: 4.40313cm x 1.88273cm
breadboards: 1

parts:
  Part1 = Arduino Nano (Rev3.0)
  R2 = Resistor [tolerance=±5% resistance=220 package=THT]
  R3 = Resistor [tolerance=±5% resistance=220 package=THT]
  R4 = Resistor [tolerance=±5% resistance=220 package=THT]

nets:
  N1: Part1.GND, R2.Pin_1, R3.Pin_1, R4.Pin_1
  N2: Part1.D10, R2.Pin_0
  N3: Part1.D11/MOSI, R3.Pin_0
  N4: Part1.D12/MISO, R4.Pin_0

notes:
  5V
  B1-
  B2-
  B3-
  B3+
  B2+
  B1+
  DIN
  GND
